# Fritzing sketch extruder (saved by Fritzing 0.9.3b)

parts:
  LED1 = LED - 3mm [color="Red (633nm)" package="3 mm [THT]"]
  LED2 = LED - 3mm [color="Green (555nm)" package="3 mm [THT]"]
  M1 = Stepper Motor - Bipolar
  M2 = Stepper Motor - Bipolar
  U1 = SWITCH-SPST-2 [package=switch-spst-vertical]
  U2 = SWITCH-SPST-2 [package=switch-spst-vertical]
  U3 = SWITCH-SPST-2 [package=switch-spst-vertical]
  S4 = Pushbutton [package="[SMD]"]
  S5 = SWITCH-SPST-2 [package=r_sw_th]
  U4 = SWITCH-SPST-2 [package=switch-spst-vertical]
  R1 = Resistor [tolerance=±5% resistance=0 package="0805 [SMD]"]
  OMRON2 = OMRON PCB Power Relay – G5LE [part_number="G5LE-1\n" package=THT]
  JACK1 = 2.1mm Barrel Jack with Terminal Block
  JACK2 = 2.1mm Barrel Jack with Terminal Block
  R2 = Temperature Sensor (Thermistor) [thermistor_type=NTC package=THT]
  U5 = SWITCH-SPST-2 [package=switch-spst-vertical]
  Part4 = EasyDriver_v44
  Part5 = EasyDriver_v44
  Part3 = Arduino Mega 2560 (Rev3)
  U6 = SWITCH-SPST-2 [package=switch-spst-vertical]
  U7 = SWITCH-SPST-2 [package=switch-spst-vertical]
  U8 = SWITCH-SPST-2 [package=switch-spst-vertical]
  U9 = SWITCH-SPST-2 [package=switch-spst-vertical]
  U10 = SWITCH-SPST-2 [package=switch-spst-vertical]
  OMRON4 = OMRON PCB Power Relay – G5LE [part_number="G5LE-1\n" package=THT]
  OMRON5 = OMRON PCB Power Relay – G5LE [part_number="G5LE-1\n" package=THT]
  OMRON6 = OMRON PCB Power Relay – G5LE [part_number="G5LE-1\n" package=THT]
  OMRON7 = OMRON PCB Power Relay – G5LE [part_number="G5LE-1\n" package=THT]
  OMRON8 = OMRON PCB Power Relay – G5LE [part_number="G5LE-1\n" package=THT]
  F1 = Fan - Ventilador [package=THT]
  F2 = Fan - Ventilador [package=THT]
  F3 = Fan - Ventilador [package=THT]
  F4 = Fan - Ventilador [package=THT]
  F5 = Fan - Ventilador [package=THT]
  R3 = Resistor [tolerance=±5% resistance=1k package="2512 [SMD]"]
  LCD1 = LCD screen
  R4 = Trimmer Potentiometer [maximum_resistance=10kΩ package=THT]
  R5 = Resistor [tolerance=±5% resistance=220 package="2512 [SMD]"]

nets:
  N1: LED1.cathode, Part3.D8_PWM
  GND: LED1.anode, LED2.anode, U1.P, U2.P, U3.P, S4.Pin_1, S4.Pin_2, U4.P, OMRON2.COIL1, U5.P, Part3.GND, U6.P, U7.P, U8.P, U9.P, U10.P, OMRON4.COIL2, OMRON5.COIL2, OMRON6.COIL2, OMRON7.COIL2, OMRON8.COIL2, R3.Pin_1, LCD1.VSS, LCD1.R/W, LCD1.LED-, R4.leg1
  N2: LED2.cathode, Part3.D9_PWM
  N3: M1.A, Part4.OUT2A
  N4: M1.C, Part4.OUT2B
  N5: M1.B, Part4.OUT1A
  N6: M1.D, Part4.OUT1B
  N7: M2.A, Part5.OUT2A
  N8: M2.C, Part5.OUT2B
  N9: M2.B, Part5.OUT1A
  N10: M2.D, Part5.OUT1B
  N11: U1.O, Part3.D11_PWM
  N12: U2.O, Part3.D12_PWM
  N13: U3.O, Part3.D10_PWM
  N14: S4.Pin_4, Part3.D27
  N15: S5.O, JACK2.NEG
  5V: S5.P, Part4.V+, Part5.V+, F1.5V, F2.5V, F3.5V, F4.5V, F5.5V
  N16: U4.O, Part3.D14/TX3
  N17: R1.Pin_0, OMRON2.B
  N18: R1.Pin_1, JACK1.POS
  N19: OMRON2.C, JACK1.NEG
  N20: OMRON2.COIL2, Part3.D26
  GND_2: JACK2.POS, Part4.GND, Part5.GND, OMRON4.B, OMRON5.B, OMRON6.B, OMRON7.B, OMRON8.B
  N21: R2.pin_0, Part3.A0, R3.Pin_0
  VCC: R2.pin_1, Part4.VCC, Part5.VCC, Part3.5V, LCD1.VDD, R4.leg2, R5.Pin_1
  N22: U5.O, Part3.D15/RX3
  N23: Part4.STEP, Part3.D6_PWM
  N24: Part4.DIR, Part3.D5_PWM
  N25: Part4.ENABLE, Part3.D7_PWM
  N26: Part5.STEP, Part3.D3_PWM
  N27: Part5.DIR, Part3.D2_PWM
  N28: Part5.ENABLE, Part3.D4_PWM
  N29: Part3.D21/SCL, OMRON5.COIL1
  N30: Part3.D20/SDA, U10.O
  N31: Part3.D19/RX1, U9.O
  N32: Part3.D18/TX1, U8.O
  N33: Part3.D17_PWM/RX2, U7.O
  N34: Part3.D16_PWM/TX2, U6.O
  N35: Part3.D22, OMRON6.COIL1
  N36: Part3.D23, OMRON4.COIL1
  N37: Part3.D24, OMRON8.COIL1
  N38: Part3.D25, OMRON7.COIL1
  N39: Part3.D45, LCD1.DB7
  N40: Part3.D47, LCD1.DB6
  N41: Part3.D49, LCD1.DB5
  N42: Part3.D51, LCD1.DB3, LCD1.DB4
  N43: Part3.D52, LCD1.RS
  N44: Part3.D53, LCD1.E
  N45: OMRON4.C, F4.GND
  N46: OMRON5.C, F1.GND
  N47: OMRON6.C, F5.GND
  N48: OMRON7.C, F2.GND
  N49: OMRON8.C, F3.GND
  N50: LCD1.V0, R4.wiper
  N51: LCD1.LED+, R5.Pin_0

notes:
  Indicadors temperatura calent/fred
  Placa base Arduino Mega 2650
  Motor de passos: extrusor
  Motor de passos: bobina
  Int: General
  Controladores motors
  tb6600
  Font d'alimentació 12V DC
  Relé d'Estat Sòlid per la resistència
  Resistènica per escalfar
  NTC
  Adaptador corrent AC-DC 220V
  Int: invertir direcció bobina
  Int: invertir direcció extrusora
  Int: rotar bobina
  Int: extrudir
  Int: escalfar
  Int: ventilador tub
  Int: ventilador controladores
  Int: ventilador bobina
  Int: ventilador arduino
  Int: ventilador filament
  STOP
  Relé vent. filament
  Relé vent. Arduino
  Relé vent. controladores
  Relé vent. bobina
  Relé vent. extrusora
  ventilador filament
  Ventilador Arduino
  Ventilador Controladores
  Ventilador bobina
  Ventilador extrusora
  LCD 16x2caràcters (16pins)
  Selector de contrast

custom parts:
  Fan - Ventilador: Ventilador de 2 pines, se encuentra comunmente en computadoras de escritorio

// code stored in the sketch: .ino
/*

  Extrusora de PLA controlada per Arduino Mega 2560.

  Projecte: 
  - https://github.com/bertugarangou/ExtrusoraPLA

  Circuit:
  - Extrusora feta per Albert Garangou,
    com a Treball de Recerca a 2n de Batxillerat,
    curs 2018/2019, tutor Jordi Fanals Oriol,
    codi amb Arduino IDE 1.8.5,

    Copyright (c) 2018 Albert Garangou Culebras (albertgarangou@gmail.com)
    This Font Software is licensed under the SIL Open Font License, Version 1.1.

*/
